# Fritzing sketch controller (saved by Fritzing 0.9.3b)

parts:
  Part1 = Thumb Joystick
  Part2 = Arduino Pro Mini (3.3V)
  Part3 = NRF24L01+ Breakout Board
  BAT1 = BC9VPC [package=bc9vpc]
  R1 = Rotary Potentiometer (Small) [maximum_resistance=100kΩ package=THT]
  R2 = Rotary Potentiometer (Small) [maximum_resistance=100kΩ package=THT]
  LED1 = LED - 5mm [color="Red (633nm)" package="5 mm [THT]"]
  S1 = Round Pushbutton
  U1 = SWITCH-SPST-2 [package=switch-spst-vertical]

nets:
  GND: Part1.GND, Part2.GND, Part3.GND, BAT1.V-
  N1: Part1.HORZ, Part2.A0
  N2: Part1.VERT, Part2.A1
  VCC: Part2.VCC, Part3.VCC
  N3: Part2.A3, R1.wiper
  N4: Part2.A2, R2.wiper
  N5: Part2.SCK, Part3.SCK
  N6: Part2.MISO, Part3.MISO
  N7: Part2.MOSI, Part3.MOSI
  N8: Part2.D9, Part3.CS
  N9: Part2.D8, Part3.CE
  N10: Part2.D7, S1.leg0
  N11: Part2.D6, LED1.anode
  N12: BAT1.V+, U1.O
