# Fritzing sketch receiver (saved by Fritzing 0.9.3b)

parts:
  Part1 = Adafruit DRV8833 DC/Stepper Motor Driver [part_number="Adafruit #3297"]
  Part2 = Arduino Pro Mini (3.3V)
  M1 = DC Motor  # not connected
  M2 = DC Motor  # not connected
  Part3 = NRF24L01+ Breakout Board
  VCC1 = 4 x AA Battery Box

nets:
  N1: Part1.PWRIN, VCC1.+
  GND: Part1.GND, Part2.GND, Part3.GND, VCC1.-
  N2: Part1.NFAULT, Part2.D2
  N3: Part1.BIN1, Part2.D10
  N4: Part1.BIN2, Part2.D3
  N5: Part1.!SLEEP, Part2.D4
  N6: Part1.AIN2, Part2.D6
  N7: Part1.AIN1, Part2.D5
  VCC: Part2.VCC, Part3.VCC
  N8: Part2.SCK, Part3.SCK
  N9: Part2.MISO, Part3.MISO
  N10: Part2.MOSI, Part3.MOSI
  N11: Part2.D9, Part3.CS
  N12: Part2.D8, Part3.CE

custom parts:
  Adafruit DRV8833 DC/Stepper Motor Driver: Spin two DC motors or step one bi-polar or uni-polar stepper with up to 1.2A per channel using the DRV8833. This motor driver chip is a nice alternative to the TB6612 driver. Like that chip, you get 2 full H-bridges, but this chip is better for low voltage uses (can run from 2.7V up to 10.8V motor power) and has built in current limiting capability. We set it up for 1A current limiting so you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
  4 x AA Battery Box: A 4 x AA battery box.
